# Fritzing sketch penghubung-lampu-laci (saved by Fritzing 0.9.2b)
circuit board: 5.5cm x 2cm
breadboards: 1

parts:
  Base = screw terminal, 3 pins
  Port0 = screw terminal, 4 pins
  Port1 = screw terminal, 4 pins
  Port2 = screw terminal, 4 pins
  Port3 = screw terminal, 4 pins
  Port4 = screw terminal, 4 pins
  Next = screw terminal, 3 pins

nets:
  N1: Base.pin1, Port0.pin1, Port1.pin1, Port2.pin1, Port3.pin1, Port4.pin1, Next.pin1
  N2: Base.pin2, Port0.pin2, Port1.pin2, Port2.pin2, Port3.pin2, Port4.pin2, Next.pin2
  N3: Base.pin3, Port0.pin3
  N4: Port0.pin4, Port1.pin3
  N5: Port1.pin4, Port2.pin3
  N6: Port2.pin4, Port3.pin3
  N7: Port3.pin4, Port4.pin3
  N8: Port4.pin4, Next.pin3

notes:
  penghubung lampu laci
  fajran © 2016
