# Fritzing sketch pengendali-lampu-laci (saved by Fritzing 0.9.2b)
circuit board: 7.11088cm x 4.43164cm
breadboards: 1

parts:
  Part1 = Arduino Nano (Rev3.0)
  J2 = female pin header, 15 pins [form="♀ (female)"]
  J1 = female pin header, 15 pins [form="♀ (female)"]
  5V_(+) = Power plug
  In0 = screw terminal, 3 pins
  In1 = screw terminal, 3 pins
  In3 = screw terminal, 3 pins
  In6 = screw terminal, 3 pins
  In7 = screw terminal, 3 pins
  In5 = screw terminal, 3 pins
  In4 = screw terminal, 3 pins
  In2 = screw terminal, 3 pins
  Out0 = screw terminal, 3 pins
  Out1 = screw terminal, 3 pins
  Out2 = screw terminal, 3 pins
  Out3 = screw terminal, 3 pins

nets:
  N1: Part1.D1/TX, J1.pin15
  N2: Part1.D0/RX, J1.pin14
  N3: Part1.RESET, J2.pin13, J1.pin13
  GND: Part1.GND, J2.pin14, J1.pin12, 5V_(+).GND, In0.pin2, In1.pin2, In3.pin2, In6.pin2, In7.pin2, In5.pin2, In4.pin2, In2.pin2, Out0.pin2, Out1.pin2, Out2.pin2, Out3.pin2
  N4: Part1.D2, J1.pin11, In0.pin3
  N5: Part1.D3, J1.pin10, In1.pin3
  N6: Part1.D4, J1.pin9, In2.pin3
  N7: Part1.D5, J1.pin8, In3.pin3
  N8: Part1.D6, J1.pin7, In4.pin3
  N9: Part1.D7, J1.pin6, In5.pin3
  N10: Part1.D8, J1.pin5, In6.pin3
  N11: Part1.D9, J1.pin4, In7.pin3
  N12: Part1.D10, J1.pin3, Out0.pin3
  N13: Part1.D11/MOSI, J1.pin2, Out1.pin3
  N14: Part1.D12/MISO, J1.pin1, Out2.pin3
  VIN: Part1.VIN, J2.pin15, 5V_(+).VCC, In0.pin1, In1.pin1, In3.pin1, In6.pin1, In7.pin1, In5.pin1, In4.pin1, In2.pin1, Out0.pin1, Out1.pin1, Out2.pin1, Out3.pin1
  N15: Part1.5V, J2.pin12
  N16: Part1.A7, J2.pin11
  N17: Part1.A6, J2.pin10
  N18: Part1.A5, J2.pin9
  N19: Part1.A4, J2.pin8
  N20: Part1.A3, J2.pin7
  N21: Part1.A2, J2.pin6
  N22: Part1.A1, J2.pin5
  N23: Part1.A0, J2.pin4
  N24: Part1.AREF, J2.pin3
  N25: Part1.3V3, J2.pin2
  N26: Part1.D13/SCK, J2.pin1, Out3.pin3

notes:
  fajran © 2016
  USB
  VIN
  GND
  lampu laci
  pengendali
  arduino nano
