# Fritzing sketch sensor-laci-dapur (saved by Fritzing 0.9.2b)
circuit board: 5cm x 1cm
breadboards: 1

parts:
  U1 = TLP621 [package=THT]
  R2 = Resistor [tolerance=±5% resistance=10k package=THT]
  R3 = Resistor [tolerance=±5% resistance=1k package=THT]
  R1 = Resistor [tolerance=±5% resistance=100 package=THT]
  E = female pin header, 2 pins [form="♀ (female)"]
  D = female pin header, 2 pins [form="♀ (female)"]
  D_2 = female pin header, 2 pins [form="♀ (female)"]
  Out_GND_+5 = screw terminal, 3 pins

nets:
  N1: U1.Pin_1, U1.Pin_4, E.pin2, D.pin1, D_2.pin1, Out_GND_+5.pin1
  N2: U1.Pin_2, R1.Pin_1, E.pin1
  N3: U1.Pin_3, R2.Pin_1, R3.Pin_0, D.pin2, D_2.pin2
  N4: R2.Pin_0, R1.Pin_0, Out_GND_+5.pin2
  N5: R3.Pin_1, Out_GND_+5.pin3

notes:
  fajran © 2016
  sensor
  laci dapur
